# Fritzing sketch jackinthebox (saved by Fritzing 0.9.3b)
breadboards: 1

parts:
  J1 = Basic Servo
  Part1 = Photon
  J2 = Piezo Speaker
  R3 = Basic Flex Resistor
  R4 = Resistor [tolerance=±5% resistance=220 package="2010 [SMD]"]

nets:
  GND: J1.gnd, Part1.GND, J2.pin1, R4.Pin_1
  VCC: J1.vcc, Part1.3V3, R3.pin_1
  N1: J1.pulse, Part1.D1
  N2: Part1.A0, R3.Pin_2, R4.Pin_0
  N3: Part1.D0, J2.pin2
